# Fritzing sketch Arduino Nano (saved by Fritzing 0.9.3b)
breadboards: 1

parts:
  Part1 = Arduino Nano (Rev3.0) (ICSP)
  R1 = Resistor [tolerance=±5% resistance=2.2k package=THT]
  J1 = female pin header, 4 pins [form="♀ (female)"]
  J2 = female pin header, 4 pins [form="♀ (female)"]
  J3 = female pin header, 4 pins [form="♀ (female)"]
  J4 = female pin header, 4 pins [form="♀ (female)"]
  R2 = Resistor [tolerance=±5% resistance=2.2k package=THT]

nets:
  N1: Part1.GND, J2.pin1, J3.pin1
  N2: Part1.D10, J1.pin4
  N3: Part1.D11/MOSI, J1.pin2
  N4: Part1.D12/MISO, J1.pin1
  N5: Part1.5V, R1.Pin_0, J2.pin4, J4.pin4, R2.Pin_0
  N6: Part1.A5, J4.pin2, R2.Pin_1
  N7: Part1.A4, R1.Pin_1, J4.pin1
  N8: Part1.D13/SCK, J1.pin3
