# Fritzing sketch Teensy2.0 (saved by Fritzing 0.9.3b)
circuit board: 8.46667cm x 5.64444cm

parts:
  Teensy1 = Teensy 2.0
  IC1 = IC, DIP package, 8 pins [chip_label=IC]

nets:
  N1: Teensy1.GND, IC1.pin5
  N2: Teensy1.B1, IC1.pin2
  N3: Teensy1.B2, IC1.pin3
  N4: Teensy1.B3, IC1.pin4
  N5: Teensy1.C7, IC1.pin1
  N6: Teensy1.VCC, IC1.pin8
