# Fritzing sketch Uno (saved by Fritzing 0.9.3b)
circuit board: 8.46667cm x 5.64444cm

parts:
  93L56R = IC, DIP package, 8 pins [chip_label=IC]
  Uno = Arduino Uno (Rev3)

nets:
  N1: 93L56R.pin1, Uno.D10_PWM/SS
  N2: 93L56R.pin2, Uno.D13/SCK
  N3: 93L56R.pin3, Uno.D11_PWM/MOSI
  N4: 93L56R.pin4, Uno.D12/MISO
  N5: 93L56R.pin5, Uno.GND
  N6: 93L56R.pin8, Uno.5V
